# Fritzing sketch coil_drive (saved by Fritzing 0.9.2b)
stripboards: 1

parts:
  P-Channel_MOSFET = Basic FET P-Channel [package="TO220 [THT]"]
  R1 = Resistor [tolerance=±10% resistance=10k package=THT]
  R2 = Resistor [tolerance=±5% resistance=10k package=THT]
  R3 = Resistor [tolerance=±5% resistance=220 package=THT]
  Q1 = 2N7000 FET N-Channel [part_number=2N7000 package=TO92]
  J1 = female pin header, 4 pins [form="♀ (female)"]

nets:
  N1: P-Channel_MOSFET.gate, R1.Pin_0, Q1.drain
  N2: P-Channel_MOSFET.drain, J1.pin3
  N3: P-Channel_MOSFET.source, R1.Pin_1, J1.pin4
  N4: R2.Pin_0, R3.Pin_1, Q1.gate
  GND: R2.Pin_1, Q1.source, J1.pin2
  N5: R3.Pin_0, J1.pin1

notes:
  Input
  Ground
  +18v
  Output

custom parts:
  2N7000 FET N-Channel: A 2N7000 MOSFET N-Channel Transistor
